# Fritzing sketch featherwing (saved by Fritzing 0.9.6b)

parts:
  Part1 = Adafruit FeatherWing Proto [part_number="Adafruit #2884"]
  U1 = 74HC04_HEX_INVERTER [package=dil14]
  Part2 = Adafruit FeatherWing Proto [part_number="Adafruit #2884"]
  R1 = Resistor [tolerance=±5% resistance=10k package="2010 [SMD]"]
  R2 = PHOTOCELL [package=photocell-kit]
  Part3 = Adafruit FeatherWing Proto [part_number="Adafruit #2884"]
  Part4 = HC-SR501 Body Sensor Module
  Part5 = Adafruit FeatherWing Proto [part_number="Adafruit #2884"]
  U2 = 74HC04_HEX_INVERTER [package=dil14]
  R3 = Resistor [tolerance=±5% resistance=10k package="2010 [SMD]"]
  R4 = PHOTOCELL [package=photocell-kit]
  Part6 = HC-SR501 Body Sensor Module
  R5 = Resistor [tolerance=±5% resistance=330 package="2010 [SMD]"]
  C5 = Electrolytic Capacitor [capacitance=1000μF voltage=35V package="1010 [SMD, electrolytic]"]

nets:
  N1: Part1.USB, Part1.N$66, Part1.N$100, U1.VCC
  GND: Part1.GND, Part1.N$129, U1.GND
  N2: Part1.K, Part1.N$116, U1.5A
  N3: Part1.N$51, Part1.N$52, Part1.N$122, U1.5Y
  N4: Part1.N$103, U1.1A
  N5: Part1.N$104, U1.1Y
  N6: Part1.N$107, U1.6A
  N7: Part1.N$110, U1.6Y
  N8: Part1.N$113, U1.2A
  N9: Part1.N$114, U1.2Y
  N10: Part1.N$119, U1.3A
  N11: Part1.N$126, U1.4Y
  N12: Part1.N$130, U1.3Y
  N13: Part1.N$133, U1.4A
  N14: Part2.J, R2.P$2
  N15: Part2.3V, R2.P$1
  N16: Part2.GND, Part2.N$123, R1.Pin_1
  N17: Part2.N$99, R1.Pin_0
  N18: Part3.3V, Part4.VCC
  GND_2: Part3.GND, Part4.GND
  N19: Part3.M, Part4.OUT
  N20: Part5.USB, Part5.N$31, Part5.N$53, Part5.N$66, Part5.N$100, U2.VCC, C5.-
  N21: Part5.M, Part6.OUT
  N22: Part5.L, Part5.N$115, Part5.N$116, U2.5A
  N23: Part5.D, R4.P$2
  N24: Part5.3V, R4.P$1, Part6.VCC
  GND_3: Part5.GND, Part5.N$129, U2.GND, R3.Pin_0, Part6.GND, C5.+
  N25: Part5.N$40, Part5.N$51, R5.Pin_0
  N26: Part5.N$73, Part5.N$122, Part5.N$123, U2.5Y, R5.Pin_1
  N27: Part5.N$79, R3.Pin_1
  N28: Part5.N$103, U2.1A
  N29: Part5.N$104, U2.1Y
  N30: Part5.N$107, U2.6A
  N31: Part5.N$110, U2.6Y
  N32: Part5.N$113, U2.2A
  N33: Part5.N$114, U2.2Y
  N34: Part5.N$119, U2.3A
  N35: Part5.N$126, U2.4Y
  N36: Part5.N$130, U2.3Y
  N37: Part5.N$133, U2.4A

notes:
  NeoPixel

custom parts:
  Adafruit FeatherWing Proto: This is the FeatherWing Proto - a prototyping add-on for all Feather boards. Using our Feather Stacking Headers or Feather Female Headers you can connect a FeatherWing on top or bottom of your Feather board and let the board take flight! This has a duplicate breakout for each pin on a Feather, as well as a bunch of plain grid proto holes. For GND and 3.3V, we give you a strip of connected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
  HC-SR501 Body Sensor Module: Pyroelectric Infrared PIR Motion Sensor Detector Module
